// Digital circuit ALU.dig as structural Verilog
module ALU (
  input  [7:0] a,
  input  [7:0] b,
  input  [3:0] funct,
  input  [3:0] flags,
  output [7:0] Out,
  output [3:0] f
);

  wire abs_driver, adder_1_c_out, adder_driver, and_driver, demultiplexer_1_out_0, demultiplexer_1_out_1,
       demultiplexer_1_out_2, demultiplexer_1_out_3, l_arithmetic_shift_driver, lrotate_driver,
       lshift_driver, or_driver, r_arithmetic_shift_driver, rrotate_driver, rshift_driver, xor_driver;
  wire [7:0] adder_1_s, and_1_out, Left_Arithmetic_out, Left_Rotate_out, Left_Shift_out, multiplexer_1_out,
       neg_1_out, or_2_out, Right_Arithmetic_out, Right_Rotate_out, Right_Shift_out, xor_1_out;

  Demultiplexer #(.Selector_Bits(4)) demultiplexer_1 (
    .sel(funct), .in(1'b1), .out_0(demultiplexer_1_out_0), .out_1(demultiplexer_1_out_1),
    .out_2(demultiplexer_1_out_2), .out_3(demultiplexer_1_out_3), .out_4(abs_driver), .out_7(and_driver),
    .out_8(or_driver), .out_9(xor_driver), .out_10(lshift_driver), .out_11(rshift_driver),
    .out_12(lrotate_driver), .out_13(rrotate_driver), .out_14(l_arithmetic_shift_driver),
    .out_15(r_arithmetic_shift_driver));  // open: out_5, out_6
  or or_1 (adder_driver, demultiplexer_1_out_0, demultiplexer_1_out_1, demultiplexer_1_out_2, demultiplexer_1_out_3);
  Neg #(.Bits(8)) neg_1 (.in(a), .out(neg_1_out));
  assign and_1_out = a & b;  // And and_1, 8 bits wide
  assign xor_1_out = a ^ b;  // XOr xor_1, 8 bits wide
  assign or_2_out = a | b;  // Or or_2, 8 bits wide
  Adder adder_1 (.a(a), .b(b), .funct(funct[1:0]), .flags(flags), .s(adder_1_s), .c_out(adder_1_c_out));
  Multiplexer #(.Bits(8)) multiplexer_1 (.sel(a[7]), .in_0(a), .in_1(neg_1_out), .out(multiplexer_1_out));
  assign Out = adder_driver ? adder_1_s : 8'bz;  // Driver driver_1
  assign f[2] = adder_driver ? adder_1_c_out : 1'bz;  // Driver driver_2
  assign Out = abs_driver ? multiplexer_1_out : 8'bz;  // Driver driver_3
  assign Out = and_driver ? and_1_out : 8'bz;  // Driver driver_4
  assign Out = xor_driver ? xor_1_out : 8'bz;  // Driver driver_5
  assign Out = or_driver ? or_2_out : 8'bz;  // Driver driver_6
  assign Out = lshift_driver ? Left_Shift_out : 8'bz;  // Driver driver_7
  assign Out = rshift_driver ? Right_Shift_out : 8'bz;  // Driver driver_8
  assign Out = lrotate_driver ? Left_Rotate_out : 8'bz;  // Driver driver_9
  assign Out = rrotate_driver ? Right_Rotate_out : 8'bz;  // Driver driver_10
  assign Out = l_arithmetic_shift_driver ? Left_Arithmetic_out : 8'bz;  // Driver driver_11
  assign Out = r_arithmetic_shift_driver ? Right_Arithmetic_out : 8'bz;  // Driver driver_12
  FlagGeneration flaggeneration_1 (.s(Out), .a(a), .b(b), .c_in(flags[2]), .c_out(f[2]), .n(f[3]), .z(f[1]), .v(f[0]));
  BarrelShifter #(.Bits(8)) Left_Shift (.in(a), .shift(4'b0001), .out(Left_Shift_out));
  BarrelShifter #(.Bits(8), .direction("right")) Right_Shift (.in(a), .shift(4'b0001), .out(Right_Shift_out));
  BarrelShifter #(.Bits(8), .barrelShifterMode("rotate")) Left_Rotate (.in(a), .shift(4'b0001), .out(Left_Rotate_out));
  BarrelShifter #(.Bits(8), .barrelShifterMode("rotate"), .direction("right")) Right_Rotate (
    .in(a), .shift(4'b0001), .out(Right_Rotate_out));
  BarrelShifter #(.Bits(8), .barrelShifterMode("arithmetic")) Left_Arithmetic (
    .in(a), .shift(4'b0001), .out(Left_Arithmetic_out));
  BarrelShifter #(.Bits(8), .barrelShifterMode("arithmetic"), .direction("right")) Right_Arithmetic (
    .in(a), .shift(4'b0001), .out(Right_Arithmetic_out));

  // Other names for the same wires on the sheet: f_v = flags[0]; f_z = flags[1]; f_c = flags[2]; f_n = flags[3]

  // Notes on the sheet:
  //   Driver Signals
  //   ALU
  //   C
  //   V
  //   N
  //   Z
endmodule
