// Digital circuit CPU.dig as structural Verilog
module CPU (
  input  in_1,
  input  clk,
  output [7:0] Data_OUT,
  output [15:0] Addr_OUT,
  output [7:0] ucode_addr,
  output [3:0] MSC
);

  wire button_1_out, Clock, counterpreset_1_ovf, demultiplexer_1_out_0, demultiplexer_1_out_1,
       Immediate_Write_Data_Bus, IR0_Read_Data_Bus, IR1_Read_Data_Bus, IR2_Read_Data_Bus,
       Memory_Output_Enable, Memory_Write_Enable, Microcode_Step_Counter_Clear, Microcode_Step_Counter_ovf,
       Program_Conter_Read_Address_Bus, Program_Conter_Write_Address_Bus, Program_Counter_Increase_Enable,
       RD_Read_Data_Bus, RD_write_Data_Bus, Read_Data_Bus, RS0_Write_Data_Bus, RS1_Write_Data_Bus, RS_Buffer,
       RS_Write_Address_Bus, segmentdriver_1_s, segmentdriver_1_t, segmentdriver_1_u, segmentdriver_1_v,
       segmentdriver_1_w, segmentdriver_1_x, segmentdriver_1_y, Write_Data_Bus;
  wire [3:0] Instruction_Flags, Instruction_RS0, Instruction_RS1, multiplexer_1_out;
  wire [5:0] uCode_3_d;
  wire [7:0] driver_3_out, driver_10_out, driver_11_out, driver_12_out, driver_13_out, Instruction_Immediate,
       ramdualport_1_d, Register_File_da, Register_File_db, uCode_2_d;
  wire [15:0] add_1_s, bitextender_1_out, counterpreset_1_out, driver_1_out, rs1_buf_q;

  Counter #(.Bits(4)) Microcode_Step_Counter (
    .en(1'b1), .C(Clock), .clr(Microcode_Step_Counter_Clear), .out(MSC), .ovf(Microcode_Step_Counter_ovf));
  LED led_1 (.in(Microcode_Step_Counter_ovf));
  EEPROM #(.AddrBits(8), .Bits(8)) uCode_3 (
    .A({ucode_addr[7:4], MSC}), .CS(1'b1), .WE(1'b0), .OE(1'b1),
    .D({Memory_Output_Enable, Memory_Write_Enable, uCode_3_d}));
  LED led_2 (.in(Addr_OUT[15]));
  EEPROM #(.AddrBits(8), .Bits(8)) uCode_2 (.A({ucode_addr[7:4], MSC}), .CS(1'b1), .WE(1'b0), .OE(1'b1), .D(uCode_2_d));
  LED led_3 (.in(Addr_OUT[11]));
  LED led_4 (.in(Addr_OUT[12]));
  LED led_5 (.in(Addr_OUT[13]));
  LED led_6 (.in(Addr_OUT[14]));
  assign driver_1_out = Program_Conter_Read_Address_Bus ? Addr_OUT : 16'bz;  // Driver driver_1
  CounterPreset #(.Bits(16)) counterpreset_1 (
    .en(Program_Counter_Increase_Enable), .C(Clock), .dir(1'b0), .in(driver_1_out),
    .ld(Program_Conter_Read_Address_Bus), .clr(1'b0), .out(counterpreset_1_out), .ovf(counterpreset_1_ovf));
  LED led_7 (.in(counterpreset_1_ovf));
  assign Addr_OUT = Program_Conter_Write_Address_Bus ? counterpreset_1_out : 16'bz;  // Driver driver_2
  LED led_8 (.in(Addr_OUT[7]));
  LED led_9 (.in(Addr_OUT[9]));
  LED led_10 (.in(Addr_OUT[8]));
  LED led_11 (.in(Addr_OUT[10]));
  EEPROM #(.AddrBits(8), .Bits(8)) uCode_1 (
    .A({ucode_addr[7:4], MSC}), .CS(1'b1), .WE(1'b0), .OE(1'b1),
    .D({Read_Data_Bus, Write_Data_Bus, Immediate_Write_Data_Bus, RS_Buffer, RS_Write_Address_Bus, RS1_Write_Data_Bus, RS0_Write_Data_Bus, RD_Read_Data_Bus}));
  LED led_12 (.in(Addr_OUT[3]));
  LED led_13 (.in(Addr_OUT[4]));
  LED led_14 (.in(Addr_OUT[5]));
  LED led_15 (.in(Addr_OUT[6]));
  RAMDualPort #(.AddrBits(15), .Bits(8)) ramdualport_1 (
    .A(Addr_OUT[14:0]), .Din(Data_OUT), .str(Memory_Write_Enable), .C(Clock), .ld(demultiplexer_1_out_1),
    .D(ramdualport_1_d));
  EEPROM #(.AddrBits(15), .Bits(8)) eeprom_1 (
    .A(Addr_OUT[14:0]), .CS(1'b1), .WE(1'b0), .OE(demultiplexer_1_out_0), .D(ramdualport_1_d));
  LED led_16 (.in(Addr_OUT[0]));
  LED led_17 (.in(Addr_OUT[1]));
  LED led_18 (.in(Addr_OUT[2]));
  EEPROM #(.AddrBits(8), .Bits(8)) uCode_0 (
    .A({ucode_addr[7:4], MSC}), .CS(1'b1), .WE(1'b0), .OE(1'b1),
    .D({RD_write_Data_Bus, IR2_Read_Data_Bus, IR1_Read_Data_Bus, IR0_Read_Data_Bus, Program_Conter_Read_Address_Bus, Program_Conter_Write_Address_Bus, Program_Counter_Increase_Enable, Microcode_Step_Counter_Clear}));
  Demultiplexer demultiplexer_1 (
    .sel(Addr_OUT[15]), .in(Memory_Output_Enable), .out_0(demultiplexer_1_out_0),
    .out_1(demultiplexer_1_out_1));
  assign driver_3_out = Read_Data_Bus ? ramdualport_1_d : 8'bz;  // Driver driver_3
  assign driver_3_out = RD_write_Data_Bus ? Register_File_db : 8'bz;  // Driver driver_4
  assign Addr_OUT = RS_Write_Address_Bus ? add_1_s : 16'bz;  // Driver driver_5
  assign Data_OUT = Write_Data_Bus ? driver_3_out : 8'bz;  // Driver driver_6
  assign driver_3_out = Immediate_Write_Data_Bus ? Instruction_Immediate : 8'bz;  // Driver driver_7
  assign driver_3_out = RS1_Write_Data_Bus ? Register_File_db : 8'bz;  // Driver driver_8
  Add #(.Bits(16)) add_1 (.a(bitextender_1_out), .b(rs1_buf_q), .c_i(1'b0), .s(add_1_s));  // open: c_o
  Clock clock_1 (.CLK(clk), .MODE(in_1), .STEP(button_1_out), .SIGNAL(Clock));
  Button button_1 (.out(button_1_out));
  Multiplexer #(.Bits(4)) multiplexer_1 (
    .sel(RD_write_Data_Bus), .in_0(Instruction_RS1), .in_1(Instruction_Flags), .out(multiplexer_1_out));
  assign driver_3_out = RS0_Write_Data_Bus ? Register_File_da : 8'bz;  // Driver driver_9
  BitExtender bitextender_1 (.in(Instruction_Immediate), .out(bitextender_1_out));
  Register #(.Bits(8)) IR_2 (.D(driver_10_out), .C(Clock), .en(IR2_Read_Data_Bus), .Q(Instruction_Immediate));
  assign driver_10_out = IR2_Read_Data_Bus ? driver_3_out : 8'bz;  // Driver driver_10
  Register #(.Bits(8)) rs0_buf (.D(Register_File_da), .C(Clock), .en(RS_Buffer), .Q(rs1_buf_q[15:8]));
  Register #(.Bits(8)) rs1_buf (.D(Register_File_db), .C(Clock), .en(RS_Buffer), .Q(rs1_buf_q[7:0]));
  LED led_19 (.in(Instruction_RS1[0]));
  LED led_20 (.in(Instruction_RS1[1]));
  LED led_21 (.in(Instruction_RS1[2]));
  LED led_22 (.in(Instruction_RS1[3]));
  LED led_23 (.in(Instruction_RS0[0]));
  LED led_24 (.in(Instruction_RS0[1]));
  LED led_25 (.in(Instruction_RS0[2]));
  assign driver_11_out = RD_Read_Data_Bus ? driver_3_out : 8'bz;  // Driver driver_11
  RegisterFile #(.AddrBits(4), .Bits(8)) Register_File (
    .Din(driver_11_out), .we(RD_Read_Data_Bus), .Rw(Instruction_Flags), .C(Clock), .Ra(Instruction_RS0),
    .Rb(multiplexer_1_out), .Da(Register_File_da), .Db(Register_File_db));
  LED led_26 (.in(Instruction_RS0[3]));
  Register #(.Bits(8)) IR_1 (
    .D(driver_12_out), .C(Clock), .en(IR1_Read_Data_Bus), .Q({Instruction_RS1, Instruction_RS0}));
  assign driver_12_out = IR1_Read_Data_Bus ? driver_3_out : 8'bz;  // Driver driver_12
  LED led_27 (.in(Instruction_Flags[0]));
  LED led_28 (.in(Instruction_Flags[1]));
  LED led_29 (.in(Instruction_Flags[2]));
  LED led_30 (.in(Instruction_Flags[3]));
  Register #(.Bits(8)) IR_0 (
    .D(driver_13_out), .C(Clock), .en(IR0_Read_Data_Bus), .Q({Instruction_Flags, ucode_addr[7:4]}));
  assign driver_13_out = IR0_Read_Data_Bus ? driver_3_out : 8'bz;  // Driver driver_13
  SegmentDriver segmentdriver_1 (
    .A(ucode_addr[4]), .B(ucode_addr[5]), .C(ucode_addr[6]), .D(ucode_addr[7]), .Y(segmentdriver_1_y),
    .X(segmentdriver_1_x), .W(segmentdriver_1_w), .V(segmentdriver_1_v), .U(segmentdriver_1_u),
    .T(segmentdriver_1_t), .S(segmentdriver_1_s));
  Seven_Seg seven_seg_1 (
    .a(segmentdriver_1_y), .b(segmentdriver_1_x), .c(segmentdriver_1_w), .d(segmentdriver_1_v),
    .e(segmentdriver_1_u), .f(segmentdriver_1_t), .g(segmentdriver_1_s), .dp(1'b0));

  assign ucode_addr[3:0] = MSC;

  // Other names for the same wires on the sheet: Instruction_Opcode[3:0] = ucode_addr[7:4];
  //   Instruction_Funct[3:0] = Instruction_Flags; Instruction_RD[3:0] = Instruction_Flags;
  //   DataBus_Out[7:0] = Data_OUT

  // Notes on the sheet:
  //   clk: Hz: 3
  //   This is just a little showcase, since my CPU is WIP.
  //   Later on, I'll finally make an ALU and Jumping implemented.
  //   And now I'd like to show some work i did on memory accessing on my CPU.
  //   uCode
  //   contents of uCode_3 (hex, n*v repeats v):
  //   80,80,80,13*0,80,80,80,13*0,80,80,80,13*0,80,80,80,0,80,11*0,80,80,80
  //   ,0,40
  //   Program Counter
  //   contents of uCode_1 (hex, n*v repeats v):
  //   80,80,80,13*0,80,80,80,3,12*0,80,80,80,21,12*0,80,80,80,18,89
  //   ,11*0,80,80,80,18,48
  //   contents of eeprom_1 (hex, n*v repeats v):
  //   2,0,ff,12,0,80,22,0,0,4,21,0,2,0,80,31,0,0,3,21
  //   contents of uCode_0 (hex, n*v repeats v):
  //   16,26,46,13*0,16,26,46,1,12*0,16,26,46,1,12*0,16,26,46,0,1,11*0
  //   ,16,26,46,0,81
  //   Register File
  //   Address Calculation
  //   Instruction Register
endmodule
