// Digital circuit Puter.dig as structural Verilog
module Puter (
  input  M,
  input  CLK
);

  wire CLK_t, demultiplexer_3_out_1, demultiplexer_3_out_2, demultiplexer_4_out_1, demultiplexer_4_out_2,
       IO_OE, IO_WE, Kb_H, Kb_L, MEM_OE, MEM_WE, RAM_OE, RAM_WE, ROM_OE, S_out, T_erm_WE, undriven,
       undriven_2, undriven_3, undriven_4;
  wire [1:0] MEM_SEL;
  wire [7:0] Data_In, Data_Out, pulldown_1_out;
  wire [13:0] MEM_ADDR;
  wire [15:0] keyboard_1_d;

  Clock clock_1 (.CLK(CLK), .MODE(M), .STEP(S_out), .SIGNAL(CLK_t));
  Button S (.out(S_out));
  Demultiplexer #(.Selector_Bits(4)) demultiplexer_1 (
    .sel(MEM_ADDR[5:2]), .in(IO_WE), .out_0(T_erm_WE));  // open: out_1, out_2, out_3, out_4, out_5, out_6, out_7, out_8, out_9, out_10, out_11, out_12, out_13, out_14, out_15
  PullDown #(.Bits(8)) pulldown_1 (.out(pulldown_1_out));
  Terminal terminal_1 (.D(pulldown_1_out), .C(CLK_t), .en(1'b1));
  assign pulldown_1_out = T_erm_WE ? Data_Out : 8'bz;  // Driver driver_1
  Keyboard keyboard_1 (.C(CLK_t), .en(1'b1), .D(keyboard_1_d));  // open: av
  Demultiplexer #(.Selector_Bits(4)) demultiplexer_2 (
    .sel(MEM_ADDR[5:2]), .in(IO_OE), .out_1(Kb_L), .out_2(Kb_H));  // open: out_0, out_3, out_4, out_5, out_6, out_7, out_8, out_9, out_10, out_11, out_12, out_13, out_14, out_15
  CPU cpu_1 ();
  assign Data_In = Kb_L ? keyboard_1_d[7:0] : 8'bz;  // Driver driver_2
  assign Data_In = Kb_H ? keyboard_1_d[15:8] : 8'bz;  // Driver driver_3
  EEPROM #(.AddrBits(14), .Bits(8)) eeprom_1 (.A(MEM_ADDR), .CS(1'b1), .WE(1'b0), .OE(ROM_OE), .D(Data_In));
  // Probe on undriven
  // Probe on undriven_2
  // Probe on undriven_3
  // Probe on undriven_4
  RAMDualPort #(.AddrBits(14), .Bits(8)) ramdualport_1 (
    .A(MEM_ADDR), .Din(Data_Out), .str(RAM_WE), .C(CLK_t), .ld(RAM_OE), .D(Data_In));
  or or_1 (RAM_WE, demultiplexer_3_out_1, demultiplexer_3_out_2);
  or or_2 (RAM_OE, demultiplexer_4_out_1, demultiplexer_4_out_2);
  Demultiplexer #(.Selector_Bits(2)) demultiplexer_3 (
    .sel(MEM_SEL), .in(MEM_WE), .out_1(demultiplexer_3_out_1), .out_2(demultiplexer_3_out_2), .out_3(IO_WE));  // open: out_0
  Demultiplexer #(.Selector_Bits(2)) demultiplexer_4 (
    .sel(MEM_SEL), .in(MEM_OE), .out_0(ROM_OE), .out_1(demultiplexer_4_out_1), .out_2(demultiplexer_4_out_2),
    .out_3(IO_OE));

  // Notes on the sheet:
  //   M: default 1
  //   CLK: Hz: 3
  //   Clock
  //   IO Select
  //   Terminal
  //   Keyboard
  //   CPU
  //   contents of eeprom_1 (hex, n*v repeats v):
  //   92,0,3f,a2,0,ff,9,a9,0,92,0,0,a2,0,18,e,a9,0,12,0,2,62,0,3,12
  //   ,0,ff,22,0,ff,5,21,0,d
  //   ROM
  //   Device signals
  //   RAM
endmodule
